# Fritzing sketch autoclave (saved by Fritzing 0.9.2b)
circuit board: 4.95831cm x 6.18675cm
perfboards: 1

parts:
  1500W_Burner = 1000W burner
  SSR-valve = SSR-25
  30PSI_pressure_sensor = MPX2010 pressure sensor [part_number=MPX]
  100K-pot = Temperature Sensor (Thermistor) [thermistor_type=NTC package=THT]
  100K-burner = Temperature Sensor (Thermistor) [thermistor_type=NTC package=THT]
  R3 = Resistor [tolerance=±5% resistance=4.7k package=THT]
  R4 = Resistor [tolerance=±5% resistance=1k package=THT]
  R5 = Resistor [tolerance=±5% resistance=1k package=THT]
  R6 = Resistor [tolerance=±5% resistance=4.7k package=THT]
  C1 = Electrolytic Capacitor [capacitance=10µF package="100 mil [THT, electrolytic]"]
  C2 = Electrolytic Capacitor [capacitance=10µF package="100 mil [THT, electrolytic]"]
  C3 = Ceramic Capacitor [capacitance=100nF package="100 mil [THT, multilayer]"]
  C4 = Ceramic Capacitor [capacitance=100nF package="100 mil [THT, multilayer]"]
  R8 = Resistor [tolerance=±5% resistance=1.5k package=THT]
  Thermal_fuse = FUSE [package=fuse_5mm]
  120VAC_in = Power plug
  pressure_relief_valve = Plastic Solenoid Valve
  SSR-burner = SSR-25
  R7 = Resistor [tolerance=±5% resistance=3.3k package=THT]
  AC_to_5VDC_adapter = HLK-PM01
  J2 = male pin header, 23 pins [form="♂ (male)"]
  J7 = male pin header, 2 pins [form="♂ (male)"]
  J8 = male pin header, 2 pins [form="♂ (male)"]
  J1 = male pin header, 23 pins [form="♂ (male)"]
  J9 = female pin header, 2 pins [form="♀ (female)"]
  J10 = female pin header, 2 pins [form="♀ (female)"]
  R9 = Resistor [tolerance=±5% resistance=1k package=THT]
  C5 = Electrolytic Capacitor [capacitance=10µF package="100 mil [THT, electrolytic]"]
  C6 = Ceramic Capacitor [capacitance=100nF package="100 mil [THT, multilayer]"]
  J6 = Screw terminal - 2 pins [package=THT]
  J5 = screw terminal, 3 pins
  J4 = screw terminal, 4 pins
  J11 = male pin header, 2 pins [form="♂ (male)"]
  E-Stop = Round Pushbutton
  J12 = female pin header, 2 pins [form="♀ (female)"]
  Q1 = NPN-Transistor [part_number=2n3904 package="TO92 [THT]"]
  Q2 = NPN-Transistor [part_number=2n3904 package="TO92 [THT]"]
  R12 = Resistor [tolerance=±5% resistance=330 package=THT]
  R13 = Resistor [tolerance=±5% resistance=1k package=THT]
  R14 = Resistor [tolerance=±5% resistance=1k package=THT]
  R15 = Resistor [tolerance=±5% resistance=330 package=THT]

nets:
  N1: 1500W_Burner.1, Thermal_fuse.1
  N2: 1500W_Burner.2, 120VAC_in.VCC, pressure_relief_valve.no_name_yet#2, AC_to_5VDC_adapter.AC#0
  N3: SSR-valve.T1, 120VAC_in.GND, SSR-burner.T1, AC_to_5VDC_adapter.AC#1
  N4: SSR-valve.T2, pressure_relief_valve.no_name_yet#1
  5V/ssr_burner+/ssr_valve+: SSR-valve.+, 30PSI_pressure_sensor.V+, SSR-burner.+, AC_to_5VDC_adapter.+Vo, J2.pin21, J1.pin21, J6.pin1, J5.pin1, J4.pin2, J4.pin4, R12.Pin_1, R15.Pin_1
  ssr_valve-: SSR-valve.-, J4.pin1, Q2.C, R15.Pin_0
  GND: 30PSI_pressure_sensor.GND, AC_to_5VDC_adapter.-Vo, J2.pin23, J1.pin23, J6.pin2, J5.pin3, Q1.E, Q2.E
  pressure: 30PSI_pressure_sensor.S, R7.Pin_0, J5.pin2
  N5: 100K-pot.pin_0, J10.pin2
  N6: 100K-pot.pin_1, J10.pin1
  N7: 100K-burner.pin_0, J9.pin2
  N8: 100K-burner.pin_1, J9.pin1
  N9: R3.Pin_0, R4.Pin_0, J8.pin1
  N10: R3.Pin_1, C1.+, C3.1, J1.pin4
  N11: R4.Pin_1, R5.Pin_1, J1.pin8
  N12: R5.Pin_0, R6.Pin_0, J7.pin1
  N13: R6.Pin_1, C2.+, C4.1, J1.pin5
  N14: C1.-, C2.-, C3.0, C4.0, R8.Pin_1, J7.pin2, J8.pin2, J1.pin7, C5.-, C6.0
  N15: R8.Pin_0, R7.Pin_1, R9.Pin_0
  N16: Thermal_fuse.2, SSR-burner.T2
  ssr_burner-: SSR-burner.-, J4.pin3, Q1.C, R12.Pin_0
  N17: J1.pin2, J11.pin2
  N18: J1.pin3, J11.pin1
  N19: J1.pin6, R9.Pin_1, C5.+, C6.1
  N20: J1.pin13, R13.Pin_1
  N21: J1.pin15, R14.Pin_1
  N22: E-Stop.leg0, J12.pin1
  N23: E-Stop.leg1, J12.pin2
  N24: Q1.B, R13.Pin_0
  N25: Q2.B, R14.Pin_0

notes:
  BeagleBone P9 header (closest to power and USB ports) plugs upside-down onto this header, with pin 1 (power port side) on lower-left

custom parts:
  1000W burner: Burner
  SSR-25: SPST SS relay
  MPX2010 pressure sensor: MPX2010 - MPXV2010G SERIES Motorola Preferred Device 10 kPa On-Chip Temperature Compensated & Calibrated Silicon Pressure Sensors. The MPX2010/MPXV2010G series silicon piezoresistive pressure sensors provide a very accuate and linearvoltage output — directly proportional to the applied pressure. These sensors house a single monolithic silicon die with the strain gauge and thin–film resistor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
